# Fritzing sketch FritzingDiagaram (saved by Fritzing 0.9.10b)
breadboards: 1

parts:
  R1 = Trimmer Potentiometer [maximum_resistance=10kΩ knob_status=50% power=0.5W package=THT]
  R2 = Trimmer Potentiometer [maximum_resistance=10kΩ knob_status=50% power=0.5W package=THT]
  R3 = Trimmer Potentiometer [maximum_resistance=10kΩ knob_status=50% power=0.5W package=THT]
  R4 = Trimmer Potentiometer [maximum_resistance=10kΩ knob_status=50% power=0.5W package=THT]
  R5 = Trimmer Potentiometer [maximum_resistance=10kΩ knob_status=50% power=0.5W package=THT]
  R6 = Trimmer Potentiometer [maximum_resistance=10kΩ knob_status=50% power=0.5W package=THT]
  M1 = Nucleo 144 MB1137
  BT1 = Bluetooth HC-06u [package=THT]
  SENSOR1 = Basic Force Sensing Resistor (FSR) [package=THT]
  J2 = Basic Force Sensing Resistor (FSR) [package=THT]
  J4 = Basic Force Sensing Resistor (FSR) [package=THT]
  J5 = Basic Force Sensing Resistor (FSR) [package=THT]
  J6 = Basic Force Sensing Resistor (FSR) [package=THT]
  J3 = Basic Force Sensing Resistor (FSR) [package=THT]

nets:
  GND: R1.leg1, R4.leg1, M1.GND, M1.PE2, M1.ADC_A_IN/PB1, M1.SPI_A_SCK/PA5, BT1.GND, SENSOR1.pin_0, J5.pin_0
  N1: R2.leg1, M1.SPI_A_MISO_/PA6, M1.PA6, J3.pin_0
  N2: R3.leg1, M1.SPI_A_MOSI/PA7, M1.PA7, J2.pin_0
  N3: R5.leg1, M1.PC3, M1.A2/PC3, J4.pin_0
  N4: R6.leg1, M1.PC0, M1.A1/PC0, J6.pin_0
  N5: M1.+3.3V, SENSOR1.pin_1, J2.pin_1, J4.pin_1, J5.pin_1, J6.pin_1, J3.pin_1
  +5V: M1.+5V, BT1.VCC
  N6: M1.PD5, M1.USART_B_TX/PD5, BT1.RXD
  N7: M1.PD6, M1.USART_B_RX/PD6, BT1.TXD

custom parts:
  Nucleo 144 MB1137: The STM32 Nucleo-144 boards based on the MB1137 reference board (NUCLEO-F207ZG, NUCLEO-F303ZE, NUCLEO-F412ZG, NUCLEO-F413ZH, NUCLEO-F429ZI, NUCLEO-F439ZI, NUCLEO-F446ZE, NUCLEO-F722ZE, NUCLEO-F746ZG, NUCLEO-F756ZG, NUCLEO-F767ZI and NUCLEO-H743ZI) provide an affordable and flexible way for users to try out new concepts and build prototypes with STM32 microcontrollers.
  Bluetooth HC-06u: Bluetooth HC-06 - face up, pins down 16.5mm x 37.5mm PCB
